# Fritzing sketch YUN_I2C_MOD-1016v6  (saved by Fritzing 0.9.1b)

parts:
  Part2 = Arduino Yun
  U11 = mystery part, 7 pins [chip_label=MOD-1016]

nets:
  N1: Part2.A2, U11.pin6
  N2: Part2.A3, U11.pin4
  N3: Part2.D10_PWM/SS, U11.pin2, U11.pin3
  N4: Part2.3V3, U11.pin1
  N5: Part2.GND, U11.pin7

notes:
  Note: use 3.3V not 5V
  YUN I2C MOD-1016v6
  SoftI2C
